# Fritzing sketch AutoTurntable (saved by Fritzing 0.9.9b)
breadboards: 3

parts:
  A1 = Arduino Nano (Rev3.0)
  J6 = shrouded pin header, 6 pins [form="♂ (shrouded male)"]
  J7 = shrouded pin header, 6 pins [form="♂ (shrouded male)"]
  C1 = Electrolytic Capacitor [capacitance=3.3µF voltage=50V package="100 mil [THT, electrolytic]"]
  J11 = shrouded pin header, 8 pins [form="♂ (shrouded male)"]
  U3 = ULN2003A [package="DIP16 [THT]"]
  U4 = ULN2003A [package="DIP16 [THT]"]
  J5 = male pin header, 4 pins [form="♂ (male)"]
  J3 = male pin header, 3 pins [form="♂ (male)"]
  J4 = male pin header, 3 pins [form="♂ (male)"]
  J2 = male pin header, 3 pins [form="♂ (male)"]
  J14 = male pin header, 5 pins [form="♂ (male)"]
  J13 = male pin header, 5 pins [form="♂ (male)"]
  J24 = male pin header, 3 pins [form="♂ (male)"]
  J25 = male pin header, 3 pins [form="♂ (male)"]
  J26 = male pin header, 3 pins [form="♂ (male)"]
  J27 = shrouded pin header, 16 pins [form="♂ (shrouded male)"]
  D3 = Rectifier Diode [part_number=1N007 package="300 mil [THT]"]
  D4 = Rectifier Diode [part_number=1N007 package="300 mil [THT]"]
  D6 = Rectifier Diode [part_number=1N007 package="300 mil [THT]"]
  J1 = screw terminal, 2 pins
  Q2 = Basic FET P-Channel [part_number=TIP120 package="TO220 [THT]"]
  J10 = male pin header, 5 pins [form="♂ (male)"]
  J8 = male pin header, 3 pins [form="♂ (male)"]
  J9 = male pin header, 3 pins [form="♂ (male)"]
  D2 = Rectifier Diode [part_number=1N007 package="300 mil [THT]"]
  D9 = Rectifier Diode [part_number=1N007 package="300 mil [THT]"]
  D10 = Rectifier Diode [part_number=1N007 package="300 mil [THT]"]
  D7 = Rectifier Diode [part_number=1N007 package="300 mil [THT]"]
  D8 = Rectifier Diode [part_number=1N007 package="300 mil [THT]"]
  D5 = Rectifier Diode [part_number=1N007 package="300 mil [THT]"]
  R24 = Resistor [tolerance=±5% resistance=10k power=0.25 package="0603 [SMD]"]
  R10 = Resistor [tolerance=±5% resistance=10k power=0.25 package="0603 [SMD]"]
  R12 = Resistor [tolerance=±5% resistance=10k power=0.25 package="0603 [SMD]"]
  R11 = Resistor [tolerance=±5% resistance=10k power=0.25 package="0603 [SMD]"]
  R9 = Resistor [tolerance=±5% resistance=10k power=0.25 package="0603 [SMD]"]
  C6 = Ceramic Capacitor [capacitance="100 nF" voltage=35V package="0603 [SMD, multilayer]"]
  C3 = Ceramic Capacitor [capacitance="100 nF" voltage=35V package="0603 [SMD, multilayer]"]
  C4 = Ceramic Capacitor [capacitance="100 nF" voltage=35V package="0603 [SMD, multilayer]"]
  R15 = Resistor [tolerance=±5% resistance=10k power=0.25 package="0603 [SMD]"]
  R4 = Resistor [tolerance=±5% resistance=10k power=0.25 package="0603 [SMD]"]
  R5 = Resistor [tolerance=±5% resistance=10k power=0.25 package="0603 [SMD]"]
  R7 = Resistor [tolerance=±5% resistance=10k power=0.25 package="0603 [SMD]"]
  R13 = Resistor [tolerance=±5% resistance=10k power=0.25 package="0603 [SMD]"]
  R14 = Resistor [tolerance=±5% resistance=10k power=0.25 package="0603 [SMD]"]
  C9 = Ceramic Capacitor [capacitance="100 nF" voltage=35V package="0603 [SMD, multilayer]"]
  C8 = Ceramic Capacitor [capacitance="100 nF" voltage=35V package="0603 [SMD, multilayer]"]
  R23 = Resistor [tolerance=±5% resistance=1k power=0.25 package="0603 [SMD]"]
  U8 = 74AHC1G08 [package=sot23-5]
  C13 = Ceramic Capacitor [capacitance="100 nF" voltage=35V package="0603 [SMD, multilayer]"]
  U5 = TC7SU04F [package=sot23-5]
  C11 = Ceramic Capacitor [capacitance="100 nF" voltage=35V package="0603 [SMD, multilayer]"]
  R27 = Resistor [tolerance=±5% resistance=10k power=0.25 package="0603 [SMD]"]
  R26 = Resistor [tolerance=±5% resistance=10k power=0.25 package="0603 [SMD]"]
  C2 = Ceramic Capacitor [capacitance="100 nF" voltage=35V package="0603 [SMD, multilayer]"]
  J19 = male pin header, 2 pins [form="♂ (male)"]
  J20 = male pin header, 2 pins [form="♂ (male)"]
  J17 = male pin header, 2 pins [form="♂ (male)"]
  J18 = male pin header, 2 pins [form="♂ (male)"]
  J15 = male pin header, 2 pins [form="♂ (male)"]
  C7 = Ceramic Capacitor [capacitance=1µF voltage=35V package="0805 [SMD, multilayer]"]
  U9 = Voltage Regulator - Variable [package="TO220 [THT]"]
  C14 = Ceramic Capacitor [capacitance=10µF voltage=35V package="0805 [SMD, multilayer]"]
  R30 = Resistor [tolerance=±5% resistance=10k power=0.25 package="0603 [SMD]"]
  C15 = Ceramic Capacitor [capacitance="100 nF" voltage=35V package="0603 [SMD, multilayer]"]
  C16 = Ceramic Capacitor [capacitance="100 nF" voltage=35V package="0603 [SMD, multilayer]"]
  C17 = Ceramic Capacitor [capacitance="100 nF" voltage=35V package="0603 [SMD, multilayer]"]
  C18 = Ceramic Capacitor [capacitance="100 nF" voltage=35V package="0603 [SMD, multilayer]"]
  U10 = SN74LVC1G18DBVR [package=sot-23-6]
  U11 = SN74LVC1G18DBVR [package=sot-23-6]
  U12 = SN74LVC1G18DBVR [package=sot-23-6]
  U13 = SN74LVC1G18DBVR [package=sot-23-6]
  R32 = Resistor [tolerance=±5% resistance=10k power=0.25 package="0603 [SMD]"]
  R33 = Resistor [tolerance=±5% resistance=10k power=0.25 package="0603 [SMD]"]
  U15 = ISL43210IHZ-T7A [package=sot-23-6]
  D11 = Rectifier Diode [part_number=1N007 package="300 mil [THT]"]
  C19 = Ceramic Capacitor [capacitance="100 nF" voltage=35V package="0603 [SMD, multilayer]"]
  J28 = male pin header, 3 pins [form="♂ (male)"]
  Part1 = SO16 [chip_label=SOIC18-W package=SO]  # not connected
  Part2 = SO-28W [chip_label=SOIC18-W package=SO(w)]

nets:
  GND: A1.GND, C1.-, U3.0V, U4.0V, J5.pin2, J3.pin1, J3.pin2, J3.pin3, J24.pin3, J25.pin3, J26.pin3, J27.pin16, J1.pin2, Q2.source, R24.Pin_0, R10.Pin_1, R12.Pin_1, R11.Pin_1, R9.Pin_1, C6.1, C3.0, C4.1, R15.Pin_0, R4.Pin_1, R5.Pin_1, R7.Pin_1, R13.Pin_0, R14.Pin_0, C9.0, C8.0, U8.GND, C13.1, U5.GND, C11.1, R27.Pin_0, R26.Pin_0, C2.1, C7.1, U9.GND, C14.1, R30.Pin_1, C15.0, C16.0, C17.1, C18.1, U10.GND, U11.GND, U12.GND, U13.GND, R32.Pin_1, R33.Pin_0, U15.GND, C19.1, Part2.12, Part2.27
  N1: A1.D2, Part2.17
  N2: A1.D3, Part2.16
  N3: A1.D4, Part2.15
  N4: A1.D5, Part2.14
  N5: A1.D6, Part2.28
  N6: A1.D7, U13.A
  N7: A1.D8, U12.A
  N8: A1.D9, U11.A
  N9: A1.D10, U10.A
  N10: A1.D11/MOSI, U10.S, U11.S, U12.S, U13.S
  N11: A1.D12/MISO, J11.pin4, J27.pin5
  VDD: A1.VIN, J6.pin5, J7.pin2, J7.pin5, C1.+, J11.pin1, U3.COM_-_Common, U4.COM_-_Common, J5.pin1, J2.pin1, J2.pin2, J2.pin3, J14.pin1, J13.pin1, J24.pin2, J25.pin2, J26.pin2, J27.pin2, D6.anode, D5.anode, C6.0, C3.1, C4.0, C9.1, C8.1, U8.VCC, C13.0, U5.+V, C11.0, C2.0, J17.pin1, J18.pin1, J15.pin2, C7.0, U9.OUT, C14.0, R30.Pin_0, C15.1, C16.1, C17.0, C18.0, U10.VDD, U11.VDD, U12.VDD, U13.VDD, J28.pin2, Part2.1, Part2.18
  N12: A1.A5, J5.pin4
  N13: A1.A4, J5.pin3
  N14: A1.A3, J26.pin1
  N15: A1.3V3, J4.pin1, J4.pin2, J4.pin3
  N16: A1.D13/SCK, J11.pin3, J27.pin6
  N17: J6.pin1, J6.pin3, J10.pin4, D2.cathode, U9.IN, U15.VDD, C19.0
  N18: J6.pin2, D11.cathode
  N19: J6.pin6, J27.pin14, R15.Pin_1, Part2.4
  N20: J7.pin1, J7.pin3, J27.pin7, D7.anode
  N21: J7.pin6, D9.anode
  N22: J11.pin5, R4.Pin_0
  N23: J11.pin6, R5.Pin_0
  N24: J11.pin8, R7.Pin_0
  N25: U3.In_1, U10.Y1
  N26: U3.In_2, U11.Y1
  N27: U3.In_3, U12.Y1
  N28: U3.In_4, U13.Y1
  N29: U3.Out_4, J13.pin5
  N30: U3.Out_3, J13.pin4
  N31: U3.Out_2, J13.pin3
  N32: U3.Out_1, J13.pin2
  N33: U4.In_1, U10.Y0
  N34: U4.In_2, U11.Y0
  N35: U4.In_3, U12.Y0
  N36: U4.In_4, U13.Y0
  N37: U4.Out_4, J14.pin5
  N38: U4.Out_3, J14.pin4
  N39: U4.Out_2, J14.pin3
  N40: U4.Out_1, J14.pin2
  N41: J24.pin1, J27.pin1, U5.IN, Part2.26
  N42: J25.pin1, Part2.9
  N43: J27.pin3, D3.anode
  N44: J27.pin4, D4.anode
  N45: J27.pin8, D10.anode
  N46: J27.pin9, D8.anode
  N47: J27.pin10, R14.Pin_1, J28.pin3, Part2.10
  N48: J27.pin11, R13.Pin_1, J28.pin1, Part2.11
  N49: D3.cathode, R12.Pin_0, J20.pin2, Part2.22
  N50: D4.cathode, R11.Pin_0, J19.pin2, Part2.21
  N51: D6.cathode, J20.pin1
  N52: J1.pin1, D11.anode
  N53: Q2.gate, R23.Pin_1
  N54: Q2.drain, J10.pin5, D2.anode
  N55: J10.pin1, U15.COM
  N56: J10.pin3, J8.pin2, J9.pin2
  N57: J8.pin1, U15.NC
  N58: J8.pin3, R26.Pin_1
  N59: J9.pin1, U15.NO
  N60: J9.pin3, R27.Pin_1
  N61: D9.cathode, D10.cathode, R33.Pin_1, U15.S
  N62: D7.cathode, D8.cathode, U8.B, R32.Pin_0
  N63: D5.cathode, J19.pin1
  N64: R24.Pin_1, J15.pin1, Part2.6
  N65: R10.Pin_0, J18.pin2, Part2.20
  N66: R9.Pin_0, J17.pin2, Part2.19
  N67: R23.Pin_0, U8.Y
  N68: U8.A, U5.OUT

notes:
  Power SW
  Speed SW
  Size SW
  LEDs
  PW SW
  SZ SW
  7-Seg Disp.
  7S DISP
  SOl
  Vertical Motor
  Horiz. Motor
  [
  Upper Limit
  Lower Limit
  V MTR
  H MTR
  Pause Button
  Play/Home Button
  U LIM
  L LIM
  PA BT
  PL BT
  Home Sensor
  HOME
  Pickup Sensor
  Speed Sensor
  5v DC
  3.3v DC
  GND
  SPEED
  PICKUP
  33-RPM Pot
  45-RPM Pot
  33 POT
  45 POT
  TURN MTR
  SPD SW
  Automatic Changer Comm
  _
  +5v
  Mux S16
  Mux S15
  Auto-mode indicator (Mux S12)
  5v DC in
  5v DC out
  NC
  Turntable power indicator LED
  33-RPM pot
  J12 pin 2
  45-RPM pot
  J12 pin 3
  J12 pin 4
  Q3 drain
  J10 pin 5
  Power indicator LED (5v)
  Turntable power indicator LED (J10 pin 3)
  Pause status LED (Ard. D13)
  Play status LED (Ard. D12)
  Play status LED GND
  Pause status LED GND
  Turntable power indicator LED GND
  Power indicator LED GND
  SW 1
  SW 2
  SW 3
  SW 4
  SW 5
  SW 6
  5v OUT
  GND OUT
  HOME ST OUT
  AUT ST O
  PAUSE CMD IN
  PLAY CMD IN
  MOVE ST OUT
  PAUSE ST OUT
  SPEED SW ST OUT
  Automatic Record Player v0.4 (July 2022)
  Designed by Patrick Nelson (github.com/pdnelson)
  Calibration Display Button
  CAL
  12v DC in
  Turn Motor
  SPEED SET IN
  TRN PW I
  12v DC
  -
  +
  SIZE 1 O
  SIZE 2 O
  Main 5v circuit
  ]

custom parts:
  Voltage Regulator - Variable: Variable DC Voltage Regulator
